// Logisim project Lab_4.circ as structural Verilog: 7 circuits, main circuit main
module main (
  input  A3,
  input  A0,
  input  B0,
  input  B3,
  input  C0,
  input  A2,
  input  A1,
  input  B2,
  input  B1,
  output S3,
  output S0,
  output C4,
  output S2,
  output S1
);

  wire fulladder_1_cout, fulladder_2_cout, fulladder_4_cout;

  FullAdder fulladder_1 (.A(A0), .B(B0), .Cin(C0), .S(S0), .Cout(fulladder_1_cout));
  FullAdder fulladder_2 (.A(A1), .B(B1), .Cin(fulladder_1_cout), .S(S1), .Cout(fulladder_2_cout));
  FullAdder fulladder_3 (.A(A3), .B(B3), .Cin(fulladder_4_cout), .S(S3), .Cout(C4));
  FullAdder fulladder_4 (.A(A2), .B(B2), .Cin(fulladder_2_cout), .S(S2), .Cout(fulladder_4_cout));
endmodule

module FullAdder (
  input  A,
  input  B,
  input  Cin,
  output S,
  output Cout
);

  wire and_1_out, and_2_out, xor_1_out;

  xor xor_1 (xor_1_out, A, B);
  and and_1 (and_1_out, B, A);
  and and_2 (and_2_out, xor_1_out, Cin);
  xor xor_2 (S, xor_1_out, Cin);
  or or_1 (Cout, and_1_out, and_2_out);
endmodule

module HalfAdder (
  input  in_1,
  input  in_2,
  output out_3,
  output out_4
);

  xor xor_1 (out_3, in_1, in_2);
  and and_1 (out_4, in_1, in_2);
endmodule

module NAND_OR (
  input  A,
  input  B,
  output F_NAND,
  output F_OR
);

  wire nand_1_out, nand_2_out;

  or or_1 (F_OR, A, B);
  nand nand_1 (nand_1_out, A, A);
  nand nand_2 (nand_2_out, B, B);
  nand nand_3 (F_NAND, nand_1_out, nand_2_out);
endmodule

module OperationBlock (
  input  A,
  input  B,
  input  OP1,
  input  OP0,
  output F
);

  wire and_1_out, halfadder_1_out_3, or_1_out, xor_1_out;

  and and_1 (and_1_out, A, B);
  or or_1 (or_1_out, A, B);
  xor xor_1 (xor_1_out, A, B);
  HalfAdder halfadder_1 (.in_1(A), .in_2(B), .out_3(halfadder_1_out_3));  // open: out_4
  Multiplexer #(.select(2)) multiplexer_1 (
    .in0(and_1_out), .in1(or_1_out), .in2(xor_1_out), .in3(halfadder_1_out_3), .out(F), .sel({OP1, OP0}));
endmodule

module AddSub (
  input  Sub,
  input  A0,
  input  B0,
  input  A1,
  input  B1,
  input  A2,
  input  B2,
  input  A3,
  input  B3,
  output S0,
  output S1,
  output Z,
  output S2,
  output C3,
  output N,
  output V,
  output S3,
  output C4,
  output C
);

  wire fulladder_1_cout, fulladder_2_cout, xor_1_out, xor_2_out, xor_3_out, xor_4_out;

  xor xor_1 (xor_1_out, B0, Sub);
  xor xor_2 (xor_2_out, B1, Sub);
  xor xor_3 (xor_3_out, B2, Sub);
  xor xor_4 (xor_4_out, B3, Sub);
  FullAdder fulladder_1 (.A(A0), .B(xor_1_out), .Cin(Sub), .S(S0), .Cout(fulladder_1_cout));
  FullAdder fulladder_2 (.A(A1), .B(xor_2_out), .Cin(fulladder_1_cout), .S(S1), .Cout(fulladder_2_cout));
  FullAdder fulladder_3 (.A(A2), .B(xor_3_out), .Cin(fulladder_2_cout), .S(S2), .Cout(C3));
  FullAdder fulladder_4 (.A(A3), .B(xor_4_out), .Cin(C3), .S(N), .Cout(C));
  nor nor_1 (Z, S0, S1, S2, N);
  xor xor_5 (V, C3, C);

  assign C4 = C;
  assign S3 = N;
endmodule

module ALU (
  input  [3:0] A,
  input  [3:0] B,
  input  [2:0] F,
  output Z,
  output C3,
  output C4,
  output C,
  output [3:0] RESULT
);

  wire N, not_1_out, Sub, V;
  wire [0:0] xor_2_out;
  wire [3:0] addsub_1_s0, and_1_out, or_1_out, xor_1_out;

  assign and_1_out = A & B;  // AND_Gate and_1, 4 bits wide
  assign or_1_out = A | B;  // OR_Gate or_1, 4 bits wide
  assign xor_1_out = A ^ B;  // XOR_Gate xor_1, 4 bits wide
  and and_2 (Sub, F[2], not_1_out);
  AddSub addsub_1 (
    .Sub(Sub), .A0(A[0]), .B0(B[0]), .A1(A[1]), .B1(B[1]), .A2(A[2]), .B2(B[2]), .A3(A[3]), .B3(B[3]),
    .S0(addsub_1_s0[0]), .S1(addsub_1_s0[1]), .Z(Z), .S2(addsub_1_s0[2]), .C3(C3), .N(N), .V(V),
    .S3(addsub_1_s0[3]), .C4(C4), .C(C));
  xor xor_2 (xor_2_out[0], N, V);
  not not_1 (not_1_out, F[1]);
  Multiplexer #(.select(3), .width(4)) multiplexer_1 (
    .in0(addsub_1_s0), .in1(addsub_1_s0), .in2(and_1_out), .in3(or_1_out), .in4(xor_1_out),
    .in5({3'b000, xor_2_out[0]}), .in6(4'b0000), .in7(4'b0000), .out(RESULT), .sel(F));
endmodule
