// Logisim project Lab_5.circ as structural Verilog
module Task_5_Async_Counter (
  input  CLK
);

  wire Q0_q, Q1_q;

  T_Flip_Flop #(.trigger("falling")) Q0 (.T(1'b1), .clk(CLK), .Q(Q0_q));  // open: Qn, reset, preset
  T_Flip_Flop #(.trigger("falling")) Q1 (.T(1'b1), .clk(Q0_q), .Q(Q1_q));  // open: Qn, reset, preset
  T_Flip_Flop #(.trigger("falling")) Q2 (.T(1'b1), .clk(Q1_q));  // open: Q, Qn, reset, preset
endmodule

module Task_6_Sync_Counter (
  input  R,
  input  M1,
  input  M2,
  input  CLK
);

  Counter #(.max('h7), .ongoal("continue"), .width(3)) counter_1 (
    .clr(R), .load(M1), .up(M2), .clk(CLK));  // open: count, D, carry, Q
endmodule

module Task_7_Turnstile (
  input  P,
  input  J,
  input  CLK,
  output OPEN1
);

  wire and_1_out, not_1_out, or_1_out;

  not not_1 (not_1_out, P);
  and and_1 (and_1_out, not_1_out, OPEN1);
  D_Flip_Flop d_ff_1 (.D(or_1_out), .clk(CLK), .Q(OPEN1));  // open: Qn, preset, reset
  or or_1 (or_1_out, and_1_out, J);
endmodule
