// Logisim project AddSub.circ as structural Verilog: 2 circuits, main circuit AddSub
module AddSub (
  input  Sub,
  input  A0,
  input  S0,
  input  B0,
  input  A1,
  input  S1,
  input  B1,
  input  A2,
  input  S2,
  input  B2,
  input  C3,
  input  A3,
  input  S3,
  input  C4,
  input  B3
);

  wire addsub_fulladder_1_cout, addsub_fulladder_2_cout, xor_1_out, xor_2_out, xor_3_out, xor_4_out;

  xor xor_1 (xor_1_out, B0, B2);
  xor xor_2 (xor_2_out, B1, B2);
  xor xor_3 (xor_3_out, B2, B2);
  xor xor_4 (xor_4_out, B3, B2);
  AddSub_FullAdder addsub_fulladder_1 (.A(A0), .B(xor_1_out), .Cin(B2), .S(S0), .Cout(addsub_fulladder_1_cout));
  AddSub_FullAdder addsub_fulladder_2 (
    .A(A1), .B(xor_2_out), .Cin(addsub_fulladder_1_cout), .S(S1), .Cout(addsub_fulladder_2_cout));
  AddSub_FullAdder addsub_fulladder_3 (.A(A2), .B(xor_3_out), .Cin(addsub_fulladder_2_cout), .S(S2), .Cout(C3));
  AddSub_FullAdder addsub_fulladder_4 (.A(A3), .B(xor_4_out), .Cin(C3), .S(S3), .Cout(C4));

  assign Sub = B2;
endmodule

module AddSub_FullAdder (
  input  A,
  input  B,
  input  Cin,
  output S,
  output Cout
);

  wire and_1_out, and_2_out, xor_1_out;

  xor xor_1 (xor_1_out, A, B);
  and and_1 (and_1_out, B, A);
  and and_2 (and_2_out, xor_1_out, Cin);
  xor xor_2 (S, xor_1_out, Cin);
  or or_1 (Cout, and_1_out, and_2_out);
endmodule
