// Logisim project Lab_6.circ as structural Verilog
module FullAdder (
  input  A,
  input  B,
  input  Cin,
  output S,
  output Cout
);

  wire and_1_out, and_2_out, xor_1_out;

  xor xor_1 (xor_1_out, A, B);
  and and_1 (and_1_out, B, A);
  and and_2 (and_2_out, xor_1_out, Cin);
  xor xor_2 (S, xor_1_out, Cin);
  or or_1 (Cout, and_1_out, and_2_out);
endmodule

module ALU (
  input  [3:0] A,
  input  [3:0] B,
  input  [2:0] F,
  output Z,
  output C3,
  output C4,
  output [3:0] RESULT
);

  wire C, N, not_1_out, or_2_out, Sub, V;
  wire [0:0] not_2_out, xor_2_out;
  wire [3:0] addsub_1_s0, and_1_out, or_1_out, xor_1_out;

  assign and_1_out = A & B;  // AND_Gate and_1, 4 bits wide
  assign or_1_out = A | B;  // OR_Gate or_1, 4 bits wide
  assign xor_1_out = A ^ B;  // XOR_Gate xor_1, 4 bits wide
  and and_2 (Sub, F[0], or_2_out);
  or or_2 (or_2_out, F[2], not_1_out);
  AddSub addsub_1 (
    .Sub(Sub), .A0(A[0]), .B0(B[0]), .A1(A[1]), .B1(B[1]), .A2(A[2]), .B2(B[2]), .A3(A[3]), .B3(B[3]),
    .S0(addsub_1_s0[0]), .S1(addsub_1_s0[1]), .Z(Z), .S2(addsub_1_s0[2]), .C3(C3), .N(N), .V(V),
    .S3(addsub_1_s0[3]), .C4(C4), .C(C));
  not not_1 (not_1_out, F[1]);
  xor xor_2 (xor_2_out[0], N, V);
  Multiplexer #(.select(3), .width(4)) multiplexer_1 (
    .in0(addsub_1_s0), .in1(addsub_1_s0), .in2(and_1_out), .in3(or_1_out), .in4(xor_1_out),
    .in5({3'b000, xor_2_out[0]}), .in6({A[2:0], 1'b0}), .in7({3'b000, not_2_out[0]}), .out(RESULT), .sel(F));
  not not_2 (not_2_out[0], C);
endmodule

module AddSub (
  input  Sub,
  input  A0,
  input  B0,
  input  A1,
  input  B1,
  input  A2,
  input  B2,
  input  A3,
  input  B3,
  output S0,
  output S1,
  output Z,
  output S2,
  output C3,
  output N,
  output V,
  output S3,
  output C4,
  output C
);

  wire fulladder_1_cout, fulladder_2_cout, xor_1_out, xor_2_out, xor_3_out, xor_4_out;

  xor xor_1 (xor_1_out, B0, Sub);
  xor xor_2 (xor_2_out, B1, Sub);
  xor xor_3 (xor_3_out, B2, Sub);
  xor xor_4 (xor_4_out, B3, Sub);
  FullAdder fulladder_1 (.A(A0), .B(xor_1_out), .Cin(Sub), .S(S0), .Cout(fulladder_1_cout));
  FullAdder fulladder_2 (.A(A1), .B(xor_2_out), .Cin(fulladder_1_cout), .S(S1), .Cout(fulladder_2_cout));
  FullAdder fulladder_3 (.A(A2), .B(xor_3_out), .Cin(fulladder_2_cout), .S(S2), .Cout(C3));
  FullAdder fulladder_4 (.A(A3), .B(xor_4_out), .Cin(C3), .S(N), .Cout(C));
  nor nor_1 (Z, S0, S1, S2, N);
  xor xor_5 (V, C3, C);

  assign C4 = C;
  assign S3 = N;
endmodule
